// Logisim project dd_proj2.circ as structural Verilog: 4 circuits, main circuit 3bitcounter
module main (
  input  in_1,
  input  in_2,
  input  in_3,
  input  in_4,
  input  in_5,
  input  in_6,
  input  in_7,
  input  in_8,
  input  in_9,
  input  in_10,
  input  in_11,
  input  in_12,
  input  in_13,
  input  in_14,
  input  in_15,
  input  in_16,
  input  in_17,
  input  in_18,
  input  in_19,
  input  in_20,
  input  in_21,
  input  in_22,
  input  in_23,
  input  in_24,
  input  in_25,
  input  in_26
);

  wire and_1_out, and_2_out, and_3_out, and_4_out, and_5_out, and_6_out, and_7_out, and_8_out, and_9_out,
       and_10_out, and_11_out, and_12_out, and_13_out, and_14_out, and_15_out, and_16_out, and_17_out,
       and_18_out, and_19_out, and_20_out, and_21_out, and_22_out, and_23_out, and_24_out, and_25_out,
       and_26_out, and_27_out, and_28_out, and_29_out, and_30_out, clock_1_out, n4bitcounter_1_out_11,
       n4bitcounter_1_q0, n4bitcounter_1_q1, n4bitcounter_1_q2, n4bitcounter_2_out_11, n4bitcounter_2_q0,
       n4bitcounter_2_q1, n4bitcounter_2_q2, n4bitcounter_3_out_11, n4bitcounter_3_q0, n4bitcounter_3_q1,
       n4bitcounter_3_q2, n4bitcounter_4_out_11, n4bitcounter_4_q0, n4bitcounter_4_q1, n4bitcounter_4_q2,
       n4bitcounter_5_out_11, n4bitcounter_5_q0, n4bitcounter_5_q1, n4bitcounter_5_q2, n4bitcounter_6_out_11,
       n4bitcounter_6_q0, n4bitcounter_6_q1, n4bitcounter_6_q2, n7seggg_1_out_5, n7seggg_1_out_6,
       n7seggg_1_out_7, n7seggg_1_out_8, n7seggg_1_out_9, n7seggg_1_out_10, n7seggg_1_out_11,
       n7seggg_2_out_5, n7seggg_2_out_6, n7seggg_2_out_7, n7seggg_2_out_8, n7seggg_2_out_9, n7seggg_2_out_10,
       n7seggg_2_out_11, n7seggg_3_out_5, n7seggg_3_out_6, n7seggg_3_out_7, n7seggg_3_out_8, n7seggg_3_out_9,
       n7seggg_3_out_10, n7seggg_3_out_11, n7seggg_4_out_5, n7seggg_4_out_6, n7seggg_4_out_7,
       n7seggg_4_out_8, n7seggg_4_out_9, n7seggg_4_out_10, n7seggg_4_out_11, n7seggg_5_out_5,
       n7seggg_5_out_6, n7seggg_5_out_7, n7seggg_5_out_8, n7seggg_5_out_9, n7seggg_5_out_10,
       n7seggg_5_out_11, n7seggg_6_out_5, n7seggg_6_out_6, n7seggg_6_out_7, n7seggg_6_out_8, n7seggg_6_out_9,
       n7seggg_6_out_10, n7seggg_6_out_11, or_1_out, or_2_out, or_3_out, or_4_out, or_5_out, or_6_out;

  and and_1 (and_1_out, in_19, in_5);
  or or_1 (or_1_out, and_12_out, in_5);
  and and_2 (and_2_out, in_23, in_5);
  and and_3 (and_3_out, in_20, in_5);
  and and_4 (and_4_out, in_24, in_5);
  and and_5 (and_5_out, in_21, in_5);
  and and_6 (and_6_out, in_25, in_5);
  and and_7 (and_7_out, in_22, in_5);
  and and_8 (and_8_out, in_26, in_5);
  _4bitcounter u_4bitcounter_1 (
    .Q0(n4bitcounter_1_q0), .Q1(n4bitcounter_1_q1), .en(or_2_out), .Q2(n4bitcounter_1_q2), .load(or_1_out),
    .D1(and_8_out), .D2(and_6_out), .D3(and_4_out), .in_4(and_2_out), .out_11(n4bitcounter_1_out_11),
    .in_1(clock_1_out));
  and and_9 (and_9_out, in_15, in_5);
  _7seggg u_7seggg_1 (
    .in_1(n4bitcounter_1_out_11), .in_2(n4bitcounter_1_q2), .in_3(n4bitcounter_1_q1),
    .in_4(n4bitcounter_1_q0), .out_5(n7seggg_1_out_5), .out_6(n7seggg_1_out_6), .out_7(n7seggg_1_out_7),
    .out_8(n7seggg_1_out_8), .out_9(n7seggg_1_out_9), .out_10(n7seggg_1_out_10), .out_11(n7seggg_1_out_11));
  _7_Segment_Display u_7_segment_display_1 (
    .g(n7seggg_1_out_11), .f(n7seggg_1_out_10), .a(n7seggg_1_out_5), .b(n7seggg_1_out_6),
    .e(n7seggg_1_out_9), .d(n7seggg_1_out_8), .c(n7seggg_1_out_7));  // open: dp
  and and_10 (and_10_out, in_16, in_5);
  or or_2 (or_2_out, in_5, and_14_out, and_12_out);
  and and_11 (and_11_out, in_17, in_5);
  or or_3 (or_3_out, and_15_out, in_5);
  and and_12 (and_12_out, n4bitcounter_1_q1, n4bitcounter_2_q2);
  and and_13 (and_13_out, in_18, in_5);
  _4bitcounter u_4bitcounter_2 (
    .Q0(n4bitcounter_2_q0), .Q1(n4bitcounter_2_q1), .en(or_3_out), .Q2(n4bitcounter_2_q2), .load(or_2_out),
    .D1(and_7_out), .D2(and_5_out), .D3(and_3_out), .in_4(and_1_out), .out_11(n4bitcounter_2_out_11),
    .in_1(clock_1_out));
  and and_14 (and_14_out, n4bitcounter_2_out_11, n4bitcounter_2_q1);
  _4bitcounter u_4bitcounter_3 (
    .Q0(n4bitcounter_3_q0), .Q1(n4bitcounter_3_q1), .en(or_4_out), .Q2(n4bitcounter_3_q2), .load(or_3_out),
    .D1(and_13_out), .D2(and_11_out), .D3(and_10_out), .in_4(and_9_out), .out_11(n4bitcounter_3_out_11),
    .in_1(clock_1_out));
  and and_15 (and_15_out, n4bitcounter_3_q2, n4bitcounter_3_q1);
  _7seggg u_7seggg_2 (
    .in_1(n4bitcounter_2_out_11), .in_2(n4bitcounter_2_q2), .in_3(n4bitcounter_2_q1),
    .in_4(n4bitcounter_2_q0), .out_5(n7seggg_2_out_5), .out_6(n7seggg_2_out_6), .out_7(n7seggg_2_out_7),
    .out_8(n7seggg_2_out_8), .out_9(n7seggg_2_out_9), .out_10(n7seggg_2_out_10), .out_11(n7seggg_2_out_11));
  _7_Segment_Display u_7_segment_display_2 (
    .g(n7seggg_2_out_11), .f(n7seggg_2_out_10), .a(n7seggg_2_out_5), .b(n7seggg_2_out_6),
    .e(n7seggg_2_out_9), .d(n7seggg_2_out_8), .c(n7seggg_2_out_7));  // open: dp
  and and_16 (and_16_out, in_11, in_5);
  _7seggg u_7seggg_3 (
    .in_1(n4bitcounter_3_out_11), .in_2(n4bitcounter_3_q2), .in_3(n4bitcounter_3_q1),
    .in_4(n4bitcounter_3_q0), .out_5(n7seggg_3_out_5), .out_6(n7seggg_3_out_6), .out_7(n7seggg_3_out_7),
    .out_8(n7seggg_3_out_8), .out_9(n7seggg_3_out_9), .out_10(n7seggg_3_out_10), .out_11(n7seggg_3_out_11));
  _7_Segment_Display u_7_segment_display_3 (
    .g(n7seggg_3_out_11), .f(n7seggg_3_out_10), .a(n7seggg_3_out_5), .b(n7seggg_3_out_6),
    .e(n7seggg_3_out_9), .d(n7seggg_3_out_8), .c(n7seggg_3_out_7));  // open: dp
  and and_17 (and_17_out, in_12, in_5);
  or or_4 (or_4_out, and_20_out, in_5);
  and and_18 (and_18_out, in_13, in_5);
  and and_19 (and_19_out, in_14, in_5);
  _4bitcounter u_4bitcounter_4 (
    .Q0(n4bitcounter_4_q0), .Q1(n4bitcounter_4_q1), .en(or_5_out), .Q2(n4bitcounter_4_q2), .load(or_4_out),
    .D1(and_19_out), .D2(and_18_out), .D3(and_17_out), .in_4(and_16_out), .out_11(n4bitcounter_4_out_11),
    .in_1(clock_1_out));
  and and_20 (and_20_out, n4bitcounter_4_out_11, n4bitcounter_4_q1);
  _7seggg u_7seggg_4 (
    .in_1(n4bitcounter_4_out_11), .in_2(n4bitcounter_4_q2), .in_3(n4bitcounter_4_q1),
    .in_4(n4bitcounter_4_q0), .out_5(n7seggg_4_out_5), .out_6(n7seggg_4_out_6), .out_7(n7seggg_4_out_7),
    .out_8(n7seggg_4_out_8), .out_9(n7seggg_4_out_9), .out_10(n7seggg_4_out_10), .out_11(n7seggg_4_out_11));
  _7_Segment_Display u_7_segment_display_4 (
    .g(n7seggg_4_out_11), .f(n7seggg_4_out_10), .a(n7seggg_4_out_5), .b(n7seggg_4_out_6),
    .e(n7seggg_4_out_9), .d(n7seggg_4_out_8), .c(n7seggg_4_out_7));  // open: dp
  and and_21 (and_21_out, in_7, in_5);
  and and_22 (and_22_out, in_8, in_5);
  or or_5 (or_5_out, and_25_out, in_5);
  and and_23 (and_23_out, in_9, in_5);
  and and_24 (and_24_out, in_10, in_5);
  _4bitcounter u_4bitcounter_5 (
    .Q0(n4bitcounter_5_q0), .Q1(n4bitcounter_5_q1), .en(or_6_out), .Q2(n4bitcounter_5_q2), .load(or_5_out),
    .D1(and_24_out), .D2(and_23_out), .D3(and_22_out), .in_4(and_21_out), .out_11(n4bitcounter_5_out_11),
    .in_1(clock_1_out));
  and and_25 (and_25_out, n4bitcounter_5_q2, n4bitcounter_5_q1);
  and and_26 (and_26_out, in_1, in_5);
  Clock clock_1 (.out(clock_1_out));
  and and_27 (and_27_out, in_2, in_5);
  _7seggg u_7seggg_5 (
    .in_1(n4bitcounter_5_out_11), .in_2(n4bitcounter_5_q2), .in_3(n4bitcounter_5_q1),
    .in_4(n4bitcounter_5_q0), .out_5(n7seggg_5_out_5), .out_6(n7seggg_5_out_6), .out_7(n7seggg_5_out_7),
    .out_8(n7seggg_5_out_8), .out_9(n7seggg_5_out_9), .out_10(n7seggg_5_out_10), .out_11(n7seggg_5_out_11));
  and and_28 (and_28_out, in_3, in_5);
  _7_Segment_Display u_7_segment_display_5 (
    .g(n7seggg_5_out_11), .f(n7seggg_5_out_10), .a(n7seggg_5_out_5), .b(n7seggg_5_out_6),
    .e(n7seggg_5_out_9), .d(n7seggg_5_out_8), .c(n7seggg_5_out_7));  // open: dp
  or or_6 (or_6_out, and_30_out, in_5);
  and and_29 (and_29_out, in_4, in_5);
  _4bitcounter u_4bitcounter_6 (
    .Q0(n4bitcounter_6_q0), .Q1(n4bitcounter_6_q1), .en(in_6), .Q2(n4bitcounter_6_q2), .load(or_6_out),
    .D1(and_29_out), .D2(and_28_out), .D3(and_27_out), .in_4(and_26_out), .out_11(n4bitcounter_6_out_11),
    .in_1(clock_1_out));
  and and_30 (and_30_out, n4bitcounter_6_q0, n4bitcounter_6_out_11);
  _7seggg u_7seggg_6 (
    .in_1(n4bitcounter_6_out_11), .in_2(n4bitcounter_6_q2), .in_3(n4bitcounter_6_q1),
    .in_4(n4bitcounter_6_q0), .out_5(n7seggg_6_out_5), .out_6(n7seggg_6_out_6), .out_7(n7seggg_6_out_7),
    .out_8(n7seggg_6_out_8), .out_9(n7seggg_6_out_9), .out_10(n7seggg_6_out_10), .out_11(n7seggg_6_out_11));
  _7_Segment_Display u_7_segment_display_6 (
    .g(n7seggg_6_out_11), .f(n7seggg_6_out_10), .a(n7seggg_6_out_5), .b(n7seggg_6_out_6),
    .e(n7seggg_6_out_9), .d(n7seggg_6_out_8), .c(n7seggg_6_out_7));  // open: dp
endmodule

module _3bitcounter (
  input  in_1,
  input  en,
  input  load,
  input  D1,
  input  D2,
  input  D3,
  output Q0,
  output Q1,
  output Q2
);

  wire and_1_out, and_2_out, multiplexer_1_out, multiplexer_2_out, multiplexer_3_out, xor_1_out, xor_2_out,
       xor_3_out;

  xor xor_1 (xor_1_out, en, Q0);
  D_Flip_Flop d_ff_1 (.clk(in_1), .D(multiplexer_1_out), .Q(Q0));  // open: Qn, preset, en, reset
  Multiplexer #(.enable("false")) multiplexer_1 (.in0(xor_1_out), .in1(D1), .out(multiplexer_1_out), .sel(load));
  and and_1 (and_1_out, en, Q0);
  xor xor_2 (xor_2_out, and_1_out, Q1);
  D_Flip_Flop d_ff_2 (.clk(in_1), .D(multiplexer_2_out), .Q(Q1));  // open: Qn, preset, en, reset
  Multiplexer #(.enable("false")) multiplexer_2 (.in0(xor_2_out), .in1(D2), .out(multiplexer_2_out), .sel(load));
  and and_2 (and_2_out, and_1_out, Q1);
  xor xor_3 (xor_3_out, Q2, and_2_out);
  D_Flip_Flop d_ff_3 (.clk(in_1), .D(multiplexer_3_out), .Q(Q2));  // open: Qn, preset, en, reset
  Multiplexer #(.enable("false")) multiplexer_3 (.in0(xor_3_out), .in1(D3), .out(multiplexer_3_out), .sel(load));
endmodule

module _4bitcounter (
  input  in_1,
  input  en,
  input  load,
  input  in_4,
  input  D1,
  input  D2,
  input  D3,
  output Q0,
  output Q2,
  output Q1,
  output out_11
);

  wire and_1_out, and_2_out, and_3_out, multiplexer_1_out, multiplexer_2_out, multiplexer_3_out,
       multiplexer_4_out, xor_1_out, xor_2_out, xor_3_out, xor_4_out;

  xor xor_1 (xor_1_out, en, Q0);
  Multiplexer #(.enable("false")) multiplexer_1 (.in0(xor_1_out), .in1(D1), .out(multiplexer_1_out), .sel(load));
  D_Flip_Flop d_ff_1 (.clk(in_1), .D(multiplexer_1_out), .Q(Q0));  // open: Qn, preset, en, reset
  and and_1 (and_1_out, en, Q0);
  D_Flip_Flop d_ff_2 (.clk(in_1), .D(multiplexer_2_out), .Q(Q1));  // open: Qn, preset, en, reset
  xor xor_2 (xor_2_out, and_1_out, Q1);
  Multiplexer #(.enable("false")) multiplexer_2 (.in0(xor_2_out), .in1(D2), .out(multiplexer_2_out), .sel(load));
  and and_2 (and_2_out, and_1_out, Q1);
  xor xor_3 (xor_3_out, Q2, and_2_out);
  D_Flip_Flop d_ff_3 (.clk(in_1), .D(multiplexer_3_out), .Q(Q2));  // open: Qn, preset, en, reset
  Multiplexer #(.enable("false")) multiplexer_3 (.in0(xor_3_out), .in1(D3), .out(multiplexer_3_out), .sel(load));
  and and_3 (and_3_out, Q2, and_2_out);
  D_Flip_Flop d_ff_4 (.clk(in_1), .D(multiplexer_4_out), .Q(out_11));  // open: Qn, preset, en, reset
  xor xor_4 (xor_4_out, and_3_out, out_11);
  Multiplexer #(.enable("false")) multiplexer_4 (.in0(xor_4_out), .in1(in_4), .out(multiplexer_4_out), .sel(load));
endmodule

module _7seggg (
  input  in_1,
  input  in_2,
  input  in_3,
  input  in_4,
  output out_5,
  output out_6,
  output out_7,
  output out_8,
  output out_9,
  output out_10,
  output out_11
);

  wire and_1_out, and_2_out, and_3_out, and_4_out, and_5_out, and_6_out, and_7_out, and_8_out, and_9_out,
       and_10_out, and_11_out, and_12_out, and_13_out, and_14_out, and_15_out, and_16_out, and_17_out,
       not_1_out, not_2_out, not_3_out, not_4_out, not_5_out, not_6_out, not_7_out, not_8_out, not_9_out,
       not_10_out, not_11_out, not_12_out, not_13_out, not_14_out, not_15_out, not_16_out, not_17_out,
       not_18_out, not_19_out, not_20_out, not_21_out, or_1_out, or_2_out, or_3_out, or_4_out, or_6_out,
       or_8_out, or_9_out, or_10_out, or_11_out, or_14_out, or_15_out;

  not not_1 (not_1_out, in_2);
  not not_2 (not_2_out, in_4);
  not not_3 (not_3_out, in_3);
  not not_4 (not_4_out, in_4);
  not not_5 (not_5_out, in_3);
  not not_6 (not_6_out, in_2);
  not not_7 (not_7_out, in_4);
  not not_8 (not_8_out, in_2);
  not not_9 (not_9_out, in_3);
  not not_10 (not_10_out, in_2);
  not not_11 (not_11_out, in_4);
  not not_12 (not_12_out, in_4);
  not not_13 (not_13_out, in_3);
  not not_14 (not_14_out, in_4);
  not not_15 (not_15_out, in_4);
  not not_16 (not_16_out, in_3);
  not not_17 (not_17_out, in_2);
  not not_18 (not_18_out, in_3);
  not not_19 (not_19_out, in_4);
  and and_1 (and_1_out, not_1_out, not_2_out);
  and and_2 (and_2_out, in_2, in_4);
  not not_20 (not_20_out, in_2);
  and and_3 (and_3_out, not_3_out, not_4_out);
  or or_1 (or_1_out, not_5_out, in_4);
  and and_4 (and_4_out, not_6_out, not_7_out);
  and and_5 (and_5_out, not_8_out, in_3);
  not not_21 (not_21_out, in_4);
  and and_6 (and_6_out, in_2, not_9_out);
  and and_7 (and_7_out, not_10_out, not_11_out);
  and and_8 (and_8_out, in_3, not_12_out);
  and and_9 (and_9_out, not_13_out, not_14_out);
  and and_10 (and_10_out, in_2, not_15_out);
  and and_11 (and_11_out, in_2, not_16_out);
  and and_12 (and_12_out, not_17_out, in_3);
  and and_13 (and_13_out, in_2, not_18_out);
  and and_14 (and_14_out, in_2, not_19_out);
  or or_2 (or_2_out, and_1_out, and_2_out);
  or or_3 (or_3_out, in_1, in_3);
  or or_4 (or_4_out, not_20_out, and_3_out);
  and and_15 (and_15_out, in_3, in_3, in_4);
  or or_5 (out_7, or_1_out, in_2);
  or or_6 (or_6_out, and_4_out, and_5_out);
  and and_16 (and_16_out, in_3, not_21_out);
  and and_17 (and_17_out, and_6_out, in_4);
  or or_7 (out_9, and_7_out, and_8_out);
  or or_8 (or_8_out, and_9_out, and_10_out);
  or or_9 (or_9_out, and_11_out, in_1);
  or or_10 (or_10_out, and_12_out, and_13_out);
  or or_11 (or_11_out, and_14_out, in_1);
  or or_12 (out_5, or_2_out, or_3_out);
  or or_13 (out_6, or_4_out, and_15_out);
  or or_14 (or_14_out, or_6_out, and_16_out);
  buf or_15 (or_15_out, and_17_out);  // OR_Gate
  or or_16 (out_10, or_8_out, or_9_out);
  or or_17 (out_11, or_10_out, or_11_out);
  or or_18 (out_8, or_14_out, or_15_out);
endmodule
